# Fritzing sketch amplificador_esp (saved by Fritzing 0.9.4)
breadboards: 1

parts:
  U1 = ESP32-38PinWide [part_number=ESP32-38PinWide]
  U2 = LM 358 Dual Op-Amp [package="DIP8 [THT]"]  # not connected
  CDM = JST-B3P-VH [part_number=JST-B3P-VH package=THT]
  H1 = polarizedheader 4pin 0.156in [package=THT]
  JP1 = Header 2 [package=jst-2-pth]  # not connected
  C2 = Capacitor Polarized [package=cpol-radial-10uf-25v]  # not connected

nets:
  N1: U1.3.3, CDM.pin3, H1.pin2
  N2: U1.GND, CDM.pin1, H1.pin1

custom parts:
  ESP32-38PinWide: Generic 38-Pin ESP32 with wide format (only access to one side of pins on a breadboard) based on Stephen Lilley's HiLetgo ESP-WROOM-32 ESP32 ESP-32S Development Board.
