# Fritzing sketch Arduino_Mega (saved by Fritzing 0.9.4)
circuit board: 11.7302cm x 9.83813cm
breadboards: 1

parts:
  Componente1 = Arduino Mega 2560 (Rev3)
  U1 = LM 358 Dual Op-Amp [package="SO 08 [SMD]"]
  R1 = Resistor [tolerance=±5% resistance=220 package="2010 [SMD]"]
  R2 = Resistor [tolerance=±5% resistance=220 package="1206 [SMD]"]  # not connected
  R3 = Resistor [tolerance=±5% resistance=220 package=THT]

nets:
  N1: Componente1.GND, R3.Pin_1
  N2: Componente1.3V3, R3.Pin_0
  N3: Componente1.D0_RX0, U1.connector2, R1.Pin_0
  N4: Componente1.D1_TX0, U1.connector1
  N5: U1.connector0, R1.Pin_1
